# Fritzing sketch leaves drying temperature control  (saved by Fritzing 0.9.6b)
breadboards: 1

parts:
  Part1 = Arduino Uno (Rev3)
  AM1 = AM2302 Humidity and Temperature Sensor
  U1 = RELAY [package=relay-jzc]
  VCC1 = 4 x AAA Battery Mount
  LED4 = smd LED [color="Red (633nm)" package="0805 [SMD]"]
  LCD2004-I2C1 = LCD2004-I2C  # not connected
  LED6 = LEDs [package=led10mm]  # not connected
  LED8 = smd LED [color="Red (633nm)" package="0603 [SMD]"]

nets:
  N1: Part1.A0, AM1.DATA
  N2: Part1.D9_PWM, LED8.anode
  N3: Part1.D11_PWM/MOSI, U1.COIL1
  5V: Part1.5V, AM1.VDD
  GND: Part1.GND, AM1.GND, U1.COIL2, LED8.cathode
  N4: U1.NO, LED4.anode
  N5: U1.MAIN, VCC1.+
  N6: VCC1.-, LED4.cathode

custom parts:
  LCD2004-I2C: A standard character display with 4x20 characters. Comes in many colors with LCM2004 IIC attached.
